# Fritzing sketch domotica_01 (saved by Fritzing 0.6.5b)
breadboards: 1

parts:
  Nano1 = Arduino Nano v2.3  # not connected
  LED1 = LED - 3mm [color="Red (633nm)" package="3 mm [THT]"]
  R1 = Resistor [tolerance=±5% resistance=220 package=THT]
  T1 = LM35 Temperature Sensor [package="TO92 [THT]"]

nets:
  N1: LED1.cathode, T1.GND
  N2: LED1.anode, R1.Pin_0
